// Logisim project cpu.circ as structural Verilog: 1 circuit, main circuit main
module main (
  input  in_1
);

  wire adder_1_cout, and_2_out, and_3_out, and_4_out, and_5_out, and_6_out, and_7_out, and_9_out, and_10_out,
       and_11_out, and_12_out, and_13_out, and_14_out, and_15_out, and_16_out, and_17_out, and_18_out,
       and_19_out, and_20_out, and_21_out, and_22_out, BYTE_SRC_out, CLK, CMP_OR_SUB_out, d_ff_1_q, d_ff_2_q,
       decoder_1_out0, decoder_1_out1, decoder_1_out2, decoder_1_out3, decoder_1_out4, decoder_1_out5,
       decoder_1_out6, decoder_1_out7, decoder_1_out9, decoder_1_out10, decoder_2_out0, decoder_2_out1,
       decoder_2_out3, decoder_2_out5, decoder_2_out6, decoder_2_out7, decoder_2_out15, decoder_3_out0,
       decoder_3_out1, decoder_3_out2, decoder_3_out3, decoder_3_out4, decoder_3_out5, decoder_3_out6,
       decoder_3_out7, decoder_3_out8, decoder_3_out9, decoder_3_out10, decoder_4_out0, decoder_4_out1,
       decoder_4_out2, decoder_4_out3, decoder_4_out4, decoder_4_out5, decoder_4_out7, decoder_4_out8,
       decoder_4_out9, decoder_4_out10, decoder_4_out12, END_INST_DEBOUNCE_q, END_INST_out,
       END_READ_OR_WRITE_out, FETCHING_INSTRUCTION_out, MEM_CLK, MEM_O_EN, MEM_W_EN, MOV_OR_ALU_out,
       nand_1_out, nor_1_out, not_1_out, not_2_out, not_3_out, not_5_out, or_1_out, or_2_out, or_3_out,
       or_4_out, or_6_out, or_7_out, or_9_out, or_10_out, or_11_out, or_12_out, or_13_out, or_14_out,
       or_15_out, or_16_out, or_17_out, or_18_out, or_19_out, or_20_out, or_21_out, or_22_out, or_23_out,
       or_24_out, or_25_out, or_26_out, or_27_out, or_28_out, or_29_out, SAME_SIGN_out, subtractor_1_bout,
       WIDE_OPCODE_q, WIDE_OPCODE_READ_out, xor_1_out, xor_3_out, xor_4_out, xor_5_out, xor_6_out;
  wire [0:0] multiplexer_5_out;
  wire [1:0] not_4_out;
  wire [3:0] ARG_LATCH_q, ARG_LATCH_q_2, counter_1_q, multiplexer_4_out, multiplexer_6_out, nor_2_out,
       rom_1_data_2, rom_1_data_3;
  wire [6:0] xor_2_out, xor_2_out_3;
  wire [7:0] ACC_H_q, ACC_L_q, and_1_out, controlled_buffer_11_out, controlled_buffer_11_out_2,
       controlled_buffer_15_out, controlled_buffer_19_out, DATA, DATA_LATCH_H_q, DATA_LATCH_L_q,
       demultiplexer_1_out0, demultiplexer_1_out1, FLAGS_q, multiplexer_8_out, multiplexer_11_out,
       OPCODE_LATCH_q, rom_1_data;
  wire [14:0] multiplexer_5_out_2;
  wire [15:0] adder_1_out, adder_2_out, adder_3_out, adder_4_out, ADDRESS, ALU_IN_LATCH_q, ALU_OUT_LATCH_q,
       and_8_out, BASE_q, controlled_buffer_1_out, controlled_buffer_18_out, divider_1_out, IP_q,
       multiplexer_1_out, multiplexer_2_out, multiplexer_3_out, multiplexer_7_out, multiplexer_9_out,
       multiplexer_10_out, multiplexer_13_out, multiplexer_14_out, multiplier_1_out, or_8_out, PREV_IP_q,
       shift_register_1_p5, shifter_1_out, shifter_2_out, STB_q, STT_q, subtractor_1_out;
  wire [15:1] multiplexer_12_out;
  wire [15:7] xor_2_out_2;

  assign and_1_out = FLAGS_q & {rom_1_data_3, rom_1_data_2};  // AND_Gate and_1, 8 bits wide
  xor xor_1 (xor_1_out, CLK, d_ff_1_q);
  D_Flip_Flop d_ff_1 (.D(and_2_out), .clk(or_9_out), .Q(d_ff_1_q), .reset(in_1));  // open: Qn, preset
  and and_2 (and_2_out, CLK, d_ff_2_q);
  D_Flip_Flop d_ff_2 (.D(1'b1), .clk(CLK), .Q(d_ff_2_q), .reset(or_3_out));  // open: Qn, preset
  Register #(.width(16)) ALU_IN_LATCH (
    .D({controlled_buffer_11_out_2, controlled_buffer_11_out}), .en(decoder_3_out7),
    .clk(multiplexer_5_out[0]), .Q(ALU_IN_LATCH_q));  // open: clr
  Decoder #(.select(4)) decoder_1 (
    .out0(decoder_1_out0), .out1(decoder_1_out1), .out2(decoder_1_out2), .out3(decoder_1_out3),
    .out4(decoder_1_out4), .out5(decoder_1_out5), .out6(decoder_1_out6), .out7(decoder_1_out7),
    .out9(decoder_1_out9), .out10(decoder_1_out10), .sel(rom_1_data_3), .en(decoder_2_out5));  // open: out8, out11, out12, out13, out14, out15
  Multiplexer #(.width(16)) multiplexer_1 (
    .in0({16{1'b0}}), .in1(shift_register_1_p5), .out(multiplexer_1_out), .sel(decoder_2_out5));
  nor FETCHING_INSTRUCTION (FETCHING_INSTRUCTION_out, OPCODE_LATCH_q[0], OPCODE_LATCH_q[1], OPCODE_LATCH_q[2], OPCODE_LATCH_q[3], OPCODE_LATCH_q[4], OPCODE_LATCH_q[5], OPCODE_LATCH_q[6], OPCODE_LATCH_q[7]);
  not not_1 (not_1_out, xor_1_out);
  or or_1 (or_1_out, and_1_out[4], and_1_out[5], and_1_out[6], and_1_out[7], and_1_out[3], and_1_out[2], and_1_out[1], and_1_out[0]);
  or CMP_OR_SUB (CMP_OR_SUB_out, decoder_1_out1, decoder_1_out4);
  not not_2 (not_2_out, decoder_2_out5);
  assign controlled_buffer_1_out = not_2_out ? {16{1'b0}} : 16'bz;  // Controlled_Buffer controlled_buffer_1
  S_R_Flip_Flop END_INST_DEBOUNCE (
    .Q(END_INST_DEBOUNCE_q), .reset(or_3_out), .preset(counter_1_q[0]));  // open: S, R, clk, Qn
  or or_2 (or_2_out, or_3_out, or_9_out);
  // Shift_Register shift_register_1: pin names not known; wires that end beside it: or_2_out, 1'b1, xor_1_out, 1'b1, shift_register_1_p5[0], shift_register_1_p5[2]
  // Shift_Register shift_register_2: pin names not known; wires that end beside it: or_2_out, 1'b1, not_1_out, 1'b1, shift_register_1_p5[4], shift_register_1_p5[6], shift_register_1_p5[8], shift_register_1_p5[10], shift_register_1_p5[12], shift_register_1_p5[14], shift_register_1_p5[1], shift_register_1_p5[3], shift_register_1_p5[5], shift_register_1_p5[7], shift_register_1_p5[9], shift_register_1_p5[11], shift_register_1_p5[13], shift_register_1_p5[15]
  and and_3 (and_3_out, decoder_2_out6, or_4_out);
  nor nor_1 (nor_1_out, and_1_out[0], and_1_out[1], and_1_out[2], and_1_out[3], and_1_out[4], and_1_out[5], and_1_out[6], and_1_out[7]);
  and and_4 (and_4_out, nor_1_out, not_3_out);
  not not_3 (not_3_out, rom_1_data_3[3]);
  and and_5 (and_5_out, rom_1_data_3[3], or_1_out);
  and and_6 (and_6_out, decoder_3_out6, multiplexer_5_out[0]);
  or or_3 (or_3_out, and_6_out, END_INST_out);
  or or_4 (or_4_out, and_4_out, and_5_out);
  or or_5 (not_4_out[1], WIDE_OPCODE_q, rom_1_data_2[0]);
  assign controlled_buffer_1_out = decoder_1_out0 ? adder_1_out : 16'bz;  // Controlled_Buffer controlled_buffer_2
  Adder #(.width(16)) adder_1 (
    .a(ALU_IN_LATCH_q), .b({controlled_buffer_11_out_2, controlled_buffer_11_out}), .out(adder_1_out),
    .cout(adder_1_cout));  // open: cin
  assign controlled_buffer_1_out = CMP_OR_SUB_out ? subtractor_1_out : 16'bz;  // Controlled_Buffer controlled_buffer_3
  Subtractor #(.width(16)) subtractor_1 (
    .a(ALU_IN_LATCH_q), .b({controlled_buffer_11_out_2, controlled_buffer_11_out}), .out(subtractor_1_out),
    .bout(subtractor_1_bout));  // open: bin
  assign controlled_buffer_1_out = decoder_1_out2 ? multiplier_1_out : 16'bz;  // Controlled_Buffer controlled_buffer_4
  Multiplier #(.width(16)) multiplier_1 (
    .a(ALU_IN_LATCH_q), .b({controlled_buffer_11_out_2, controlled_buffer_11_out}), .out(multiplier_1_out));  // open: cin, cout
  assign controlled_buffer_1_out = decoder_1_out3 ? divider_1_out : 16'bz;  // Controlled_Buffer controlled_buffer_5
  Divider #(.width(16)) divider_1 (
    .a(ALU_IN_LATCH_q), .b({controlled_buffer_11_out_2, controlled_buffer_11_out}), .out(divider_1_out));  // open: upper, rem
  Shifter #(.width(16)) shifter_1 (.in(ALU_IN_LATCH_q), .\dist (controlled_buffer_11_out[3:0]), .out(shifter_1_out));
  Shifter #(.shift("lr"), .width(16)) shifter_2 (
    .in(ALU_IN_LATCH_q), .\dist (controlled_buffer_11_out[3:0]), .out(shifter_2_out));
  or END_INST (END_INST_out, in_1, and_3_out, and_7_out);
  and and_7 (and_7_out, END_INST_DEBOUNCE_q, decoder_2_out0);
  Multiplexer #(.width(16)) multiplexer_2 (
    .in0({16{1'b0}}), .in1(shift_register_1_p5), .out(multiplexer_2_out), .sel(decoder_2_out15));
  assign controlled_buffer_1_out = decoder_1_out5 ? and_8_out : 16'bz;  // Controlled_Buffer controlled_buffer_6
  assign controlled_buffer_1_out = decoder_1_out9 ? shifter_1_out : 16'bz;  // Controlled_Buffer controlled_buffer_7
  assign controlled_buffer_1_out = decoder_1_out10 ? shifter_2_out : 16'bz;  // Controlled_Buffer controlled_buffer_8
  Register OPCODE_LATCH (
    .D(controlled_buffer_11_out), .en(decoder_3_out6), .clk(multiplexer_5_out[0]), .Q(OPCODE_LATCH_q),
    .clr(END_INST_out));
  Register ARG_LATCH (
    .D(controlled_buffer_11_out_2), .en(decoder_3_out6), .clk(multiplexer_5_out[0]),
    .Q({ARG_LATCH_q_2, ARG_LATCH_q}), .clr(END_INST_out));
  S_R_Flip_Flop WIDE_OPCODE (
    .Q(WIDE_OPCODE_q), .reset(or_3_out), .preset(WIDE_OPCODE_READ_out));  // open: S, R, clk, Qn
  Register #(.width(16)) IP (.D(multiplexer_3_out), .en(or_6_out), .clk(or_7_out), .Q(IP_q), .clr(in_1));
  Multiplexer #(.width(16)) multiplexer_3 (
    .in0({controlled_buffer_11_out_2, controlled_buffer_11_out}), .in1(adder_2_out), .out(multiplexer_3_out),
    .sel(decoder_2_out15));
  or or_6 (or_6_out, decoder_2_out15, decoder_3_out4);
  or or_7 (or_7_out, multiplexer_2_out[0], multiplexer_5_out[0]);
  assign and_8_out = {controlled_buffer_11_out_2, controlled_buffer_11_out} & ALU_IN_LATCH_q;  // AND_Gate and_8, 16 bits wide
  assign or_8_out = {controlled_buffer_11_out_2, controlled_buffer_11_out} | ALU_IN_LATCH_q;  // OR_Gate or_8, 16 bits wide
  assign controlled_buffer_1_out = decoder_1_out6 ? or_8_out : 16'bz;  // Controlled_Buffer controlled_buffer_9
  assign controlled_buffer_1_out = decoder_1_out7 ? {xor_2_out_2[15], xor_2_out_3, xor_2_out_2[7], xor_2_out} : 16'bz;  // Controlled_Buffer controlled_buffer_10
  nor SAME_SIGN (SAME_SIGN_out, and_9_out, and_12_out);
  and and_9 (and_9_out, xor_2_out_2[15], ~and_17_out);  // AND_Gate
  Counter #(.max('hf), .width(4)) counter_1 (
    .clr(or_3_out), .up(1'b1), .clk(or_9_out), .Q(counter_1_q));  // open: load, count, D, carry
  not not_4 (not_4_out[0], not_4_out[1]);
  assign {controlled_buffer_11_out_2, controlled_buffer_11_out} = decoder_4_out4 ? IP_q : 16'bz;  // Controlled_Buffer controlled_buffer_11
  assign {xor_2_out_2[15], xor_2_out_3, xor_2_out_2[7], xor_2_out} = {controlled_buffer_11_out_2, controlled_buffer_11_out} ^ ALU_IN_LATCH_q;  // XOR_Gate xor_2, 16 bits wide
  and and_10 (and_10_out, ALU_IN_LATCH_q[7], and_17_out);
  and and_11 (and_11_out, ~and_17_out, ALU_IN_LATCH_q[15]);  // AND_Gate
  and and_12 (and_12_out, xor_2_out_2[7], and_17_out);
  ROM #(.addrWidth(12), .dataWidth(16)) rom_1 (
    .addr({OPCODE_LATCH_q, counter_1_q}), .data({rom_1_data_3, rom_1_data_2, rom_1_data}));
  or or_9 (or_9_out, multiplexer_2_out[0], multiplexer_10_out[0], decoder_2_out6, multiplexer_1_out[0], END_READ_OR_WRITE_out, multiplexer_5_out[0]);
  Adder #(.width(16)) adder_2 (.a({{14{1'b0}}, not_4_out}), .b(IP_q), .out(adder_2_out));  // open: cin, cout
  xor xor_3 (xor_3_out, CMP_OR_SUB_out, SAME_SIGN_out);
  or or_10 (or_10_out, and_10_out, and_11_out);
  or NEGATIVE (nor_2_out[2], and_13_out, and_14_out);
  and and_13 (and_13_out, controlled_buffer_1_out[15], ~and_17_out);  // AND_Gate
  and and_14 (and_14_out, controlled_buffer_1_out[7], and_17_out);
  assign {controlled_buffer_11_out_2, controlled_buffer_11_out} = decoder_4_out12 ? PREV_IP_q : 16'bz;  // Controlled_Buffer controlled_buffer_12
  Register #(.width(16)) PREV_IP (.D(IP_q), .en(or_6_out), .clk(or_7_out), .Q(PREV_IP_q), .clr(in_1));
  Register #(.width(16)) ALU_OUT_LATCH (
    .D(controlled_buffer_1_out), .en(1'b1), .clk(multiplexer_1_out[0]), .Q(ALU_OUT_LATCH_q));  // open: clr
  Register FLAGS (.D({4'b0000, nor_2_out}), .en(1'b1), .clk(multiplexer_1_out[0]), .Q(FLAGS_q));  // open: clr
  and OVERFLOW (nor_2_out[3], xor_3_out, xor_4_out);
  xor xor_4 (xor_4_out, or_10_out, nor_2_out[2]);
  or CARRY (nor_2_out[1], and_15_out, and_16_out);
  and and_15 (and_15_out, controlled_buffer_1_out[8], and_17_out);
  Decoder #(.enable("false"), .select(4)) decoder_2 (
    .out0(decoder_2_out0), .out1(decoder_2_out1), .out3(decoder_2_out3), .out4(MEM_O_EN),
    .out5(decoder_2_out5), .out6(decoder_2_out6), .out7(decoder_2_out7), .out15(decoder_2_out15),
    .sel(rom_1_data[3:0]));  // open: out2, out8, out9, out10, out11, out12, out13, out14
  assign {controlled_buffer_11_out_2, controlled_buffer_11_out} = decoder_4_out7 ? ALU_OUT_LATCH_q : 16'bz;  // Controlled_Buffer controlled_buffer_13
  nor nor_2 (nor_2_out[0], controlled_buffer_1_out[0], controlled_buffer_1_out[1], controlled_buffer_1_out[2], controlled_buffer_1_out[3], controlled_buffer_1_out[4], controlled_buffer_1_out[5], controlled_buffer_1_out[6], controlled_buffer_1_out[7], controlled_buffer_1_out[9], controlled_buffer_1_out[10], controlled_buffer_1_out[11], controlled_buffer_1_out[12], controlled_buffer_1_out[13], controlled_buffer_1_out[14], controlled_buffer_1_out[15], controlled_buffer_1_out[8]);
  and and_16 (and_16_out, ~and_17_out, or_11_out);  // AND_Gate
  or or_11 (or_11_out, subtractor_1_bout, adder_1_cout);
  Decoder #(.select(4)) decoder_3 (
    .out0(decoder_3_out0), .out1(decoder_3_out1), .out2(decoder_3_out2), .out3(decoder_3_out3),
    .out4(decoder_3_out4), .out5(decoder_3_out5), .out6(decoder_3_out6), .out7(decoder_3_out7),
    .out8(decoder_3_out8), .out9(decoder_3_out9), .out10(decoder_3_out10), .sel(multiplexer_4_out),
    .en(decoder_2_out1));  // open: out11, out12, out13, out14, out15
  Multiplexer #(.select(2), .width(4)) multiplexer_4 (
    .in0(rom_1_data_3), .in1(ARG_LATCH_q_2), .in2(ARG_LATCH_q), .out(multiplexer_4_out), .sel(rom_1_data[7:6]));  // open: in3
  or MOV_OR_ALU (MOV_OR_ALU_out, decoder_2_out1, decoder_2_out5);
  or BYTE_SRC (BYTE_SRC_out, decoder_4_out0, decoder_4_out1);
  Multiplexer #(.width(16)) multiplexer_5 (
    .in0({16{1'b0}}), .in1(shift_register_1_p5), .out({multiplexer_5_out_2, multiplexer_5_out[0]}),
    .sel(MOV_OR_ALU_out));
  and and_17 (and_17_out, BYTE_SRC_out, MOV_OR_ALU_out);
  Multiplexer #(.select(2), .width(4)) multiplexer_6 (
    .in0(rom_1_data_2), .in1(ARG_LATCH_q_2), .in2(ARG_LATCH_q), .out(multiplexer_6_out), .sel(rom_1_data[5:4]));  // open: in3
  Decoder #(.select(4)) decoder_4 (
    .out0(decoder_4_out0), .out1(decoder_4_out1), .out2(decoder_4_out2), .out3(decoder_4_out3),
    .out4(decoder_4_out4), .out5(decoder_4_out5), .out7(decoder_4_out7), .out8(decoder_4_out8),
    .out9(decoder_4_out9), .out10(decoder_4_out10), .out12(decoder_4_out12), .sel(multiplexer_6_out),
    .en(MOV_OR_ALU_out));  // open: out6, out11, out13, out14, out15
  and WIDE_OPCODE_READ (WIDE_OPCODE_READ_out, ~and_19_out, FETCHING_INSTRUCTION_out, multiplexer_9_out[2]);  // AND_Gate
  Multiplexer #(.width(16)) multiplexer_7 (
    .in0({controlled_buffer_11_out_2, controlled_buffer_11_out}), .in1(adder_3_out), .out(multiplexer_7_out),
    .sel(or_12_out));
  or or_12 (or_12_out, multiplexer_9_out[0], MEM_W_EN);
  or END_READ_OR_WRITE (END_READ_OR_WRITE_out, or_19_out, or_13_out);
  or or_13 (or_13_out, and_18_out, and_19_out);
  and and_18 (and_18_out, ~rom_1_data_2[0], ~FETCHING_INSTRUCTION_out, or_14_out);  // AND_Gate
  or or_14 (or_14_out, multiplexer_12_out[1], multiplexer_9_out[0]);
  Multiplexer #(.width(8)) multiplexer_8 (
    .in0(controlled_buffer_11_out), .in1(controlled_buffer_11_out_2), .out(multiplexer_8_out),
    .sel(decoder_3_out2));
  Register #(.width(16)) ADDR_LATCH (.D(multiplexer_7_out), .en(or_15_out), .clk(or_16_out), .Q(ADDRESS));  // open: clr
  or or_15 (or_15_out, decoder_3_out5, multiplexer_9_out[0], multiplexer_12_out[1]);
  or or_16 (or_16_out, multiplexer_9_out[1], multiplexer_12_out[2], multiplexer_5_out[0]);
  and and_19 (and_19_out, FETCHING_INSTRUCTION_out, multiplexer_9_out[1], nand_1_out);
  nand nand_1 (nand_1_out, DATA_LATCH_L_q[6], DATA_LATCH_L_q[7]);
  Register ACC_L (.D(controlled_buffer_11_out), .en(or_17_out), .clk(multiplexer_5_out[0]), .Q(ACC_L_q));  // open: clr
  or or_17 (or_17_out, decoder_3_out0, decoder_3_out2);
  Register ACC_H (.D(multiplexer_8_out), .en(or_18_out), .clk(multiplexer_5_out[0]), .Q(ACC_H_q));  // open: clr
  or or_18 (or_18_out, decoder_3_out2, decoder_3_out1);
  assign {controlled_buffer_11_out_2, controlled_buffer_11_out} = decoder_4_out5 ? ADDRESS : 16'bz;  // Controlled_Buffer controlled_buffer_14
  Adder #(.width(16)) adder_3 (.a(ADDRESS), .b(16'h1), .out(adder_3_out));  // open: cin, cout
  or or_19 (or_19_out, multiplexer_9_out[3], multiplexer_12_out[3]);
  Demultiplexer #(.width(8)) demultiplexer_1 (
    .out0(demultiplexer_1_out0), .out1(demultiplexer_1_out1), .in(ACC_H_q), .sel(decoder_4_out2));
  or or_20 (or_20_out, decoder_3_out3, and_20_out);
  and and_20 (and_20_out, MEM_O_EN, multiplexer_9_out[1]);
  Multiplexer #(.width(16)) multiplexer_9 (
    .in0({16{1'b0}}), .in1(shift_register_1_p5), .out(multiplexer_9_out), .sel(MEM_O_EN));
  assign controlled_buffer_15_out = not_5_out ? ACC_L_q : 8'bz;  // Controlled_Buffer controlled_buffer_15
  not not_5 (not_5_out, decoder_4_out1);
  assign controlled_buffer_15_out = decoder_4_out1 ? demultiplexer_1_out0 : 8'bz;  // Controlled_Buffer controlled_buffer_16
  Clock clock_1 (.out(CLK));
  or or_21 (or_21_out, decoder_3_out3, and_21_out);
  and and_21 (and_21_out, ~multiplexer_9_out[1], MEM_O_EN);  // AND_Gate
  xor xor_5 (xor_5_out, multiplexer_9_out[1], multiplexer_9_out[0]);
  assign {controlled_buffer_11_out_2, controlled_buffer_11_out} = or_22_out ? {demultiplexer_1_out1, controlled_buffer_15_out} : 16'bz;  // Controlled_Buffer controlled_buffer_17
  or or_22 (or_22_out, decoder_4_out0, decoder_4_out1, decoder_4_out2);
  assign controlled_buffer_18_out = decoder_3_out3 ? {controlled_buffer_11_out_2, controlled_buffer_11_out} : 16'bz;  // Controlled_Buffer controlled_buffer_18
  or or_23 (or_23_out, multiplexer_5_out[0], xor_5_out, multiplexer_9_out[3]);
  Register DATA_LATCH_L (
    .D(controlled_buffer_18_out[7:0]), .en(or_21_out), .clk(or_23_out), .Q(DATA_LATCH_L_q));  // open: clr
  Register DATA_LATCH_H (
    .D(controlled_buffer_18_out[15:8]), .en(or_20_out), .clk(or_23_out), .Q(DATA_LATCH_H_q), .clr(and_22_out));
  and and_22 (and_22_out, or_21_out, xor_5_out);
  Multiplexer #(.width(16)) multiplexer_10 (
    .in0({16{1'b0}}), .in1(shift_register_1_p5), .out(multiplexer_10_out), .sel(decoder_2_out7));
  Multiplexer #(.width(8)) multiplexer_11 (
    .in0(DATA_LATCH_L_q), .in1(DATA_LATCH_H_q), .out(multiplexer_11_out), .sel(or_24_out));
  Demultiplexer #(.disabled("Z"), .tristate("true"), .width(8)) demultiplexer_2 (
    .out0(controlled_buffer_18_out[7:0]), .out1(controlled_buffer_18_out[15:8]),
    .in(controlled_buffer_19_out), .sel(or_24_out));
  assign controlled_buffer_19_out = MEM_O_EN ? DATA : 8'bz;  // Controlled_Buffer controlled_buffer_19
  or or_24 (or_24_out, or_20_out, multiplexer_12_out[2]);
  or or_25 (or_25_out, decoder_3_out9, decoder_2_out7);
  or or_26 (or_26_out, multiplexer_10_out[0], multiplexer_5_out[0]);
  assign DATA = MEM_W_EN ? multiplexer_11_out : 8'bz;  // Controlled_Buffer controlled_buffer_20
  or or_27 (or_27_out, multiplexer_12_out[3], multiplexer_9_out[2]);
  Multiplexer #(.width(16)) multiplexer_12 (
    .in0({16{1'b0}}), .in1(shift_register_1_p5), .out({multiplexer_12_out, MEM_W_EN}), .sel(decoder_2_out3));
  Register #(.width(16)) STT (.D(multiplexer_13_out), .en(or_25_out), .clk(or_26_out), .Q(STT_q));  // open: clr
  Multiplexer #(.width(16)) multiplexer_13 (
    .in0({controlled_buffer_11_out_2, controlled_buffer_11_out}), .in1(adder_4_out),
    .out(multiplexer_13_out), .sel(decoder_2_out7));
  assign {controlled_buffer_11_out_2, controlled_buffer_11_out} = decoder_4_out3 ? {DATA_LATCH_H_q, DATA_LATCH_L_q} : 16'bz;  // Controlled_Buffer controlled_buffer_21
  or or_28 (or_28_out, multiplexer_9_out[0], multiplexer_12_out[2]);
  Multiplexer #(.width(16)) multiplexer_14 (
    .in0(16'hfffe), .in1(16'h2), .out(multiplexer_14_out), .sel(rom_1_data_2[0]));
  Register #(.width(16)) STB (
    .D({controlled_buffer_11_out_2, controlled_buffer_11_out}), .en(decoder_3_out10),
    .clk(multiplexer_5_out[0]), .Q(STB_q));  // open: clr
  Register #(.width(16)) BASE (
    .D({controlled_buffer_11_out_2, controlled_buffer_11_out}), .en(decoder_3_out8),
    .clk(multiplexer_5_out[0]), .Q(BASE_q));  // open: clr
  or or_29 (or_29_out, MEM_O_EN, multiplexer_12_out[1]);
  RAM #(.addrWidth(16), .databus("bidir")) ram_1 (
    .addr(ADDRESS), .we(MEM_W_EN), .oe(MEM_O_EN), .clk(MEM_CLK), .data(DATA));
  assign {controlled_buffer_11_out_2, controlled_buffer_11_out} = decoder_4_out9 ? STT_q : 16'bz;  // Controlled_Buffer controlled_buffer_22
  Adder #(.width(16)) adder_4 (.a(STT_q), .b(multiplexer_14_out), .out(adder_4_out));  // open: cin, cout
  assign {controlled_buffer_11_out_2, controlled_buffer_11_out} = decoder_4_out10 ? STB_q : 16'bz;  // Controlled_Buffer controlled_buffer_23
  assign {controlled_buffer_11_out_2, controlled_buffer_11_out} = decoder_4_out8 ? BASE_q : 16'bz;  // Controlled_Buffer controlled_buffer_24
  xor xor_6 (xor_6_out, or_28_out, or_29_out);
  or or_30 (MEM_CLK, or_27_out, xor_6_out);

  // Other names for the same wires on the sheet: RST = in_1

  // Notes on the sheet:
  //   contents of rom_1 (hex, n*v repeats v):
  //   5401 4 f 6301 12*0 5401 4 301 f 12*0 101 15*0 5401 4 1301 f 12*0 1001 15*0 5401 104 2301 10f 12*0
  //   2801 15*0 2901 15*0 2a01 15*0 5401 104 8301 10f 12*0 8201 15*0 8901 15*0 8a01 15*0 5401 104 9301 10f
  //   12*0 9201 15*0 9801 15*0 9a01 15*0 a901 15*0 5401 3 7001 305 701 f 10*0 7001 105 701 13*0 5401 3
  //   7101 305 1701 f 10*0 7101 5 1701 13*0 5401 103 7201 305 2701 10f 10*0 7201 805 2701 13*0 7201 905
  //   2701 13*0 7201 a05 2701 13*0 5401 103 7801 305 8701 10f 10*0 7801 205 8701 13*0 7801 905 8701 13*0
  //   7801 a05 8701 13*0 5401 103 7901 305 9701 10f 10*0 7901 205 9701 13*0 7901 805 9701 13*0 5401 3 7001
  //   1305 701 f 10*0 7001 1105 701 13*0 5401 3 7101 1305 1701 f 10*0 7101 1005 1701 13*0 5401 104 7201
  //   1305 2701 10f 10*0 7201 1805 2701 13*0 7201 1905 2701 13*0 7201 1a05 2701 13*0 5401 103 7801 1305
  //   8701 10f 10*0 7801 1205 8701 13*0 7801 1905 8701 13*0 7801 1a05 8701 13*0 5401 103 7901 1305 9701
  //   10f 10*0 7901 1205 9701 13*0 7901 1805 9701 205*0 5401 3 7001 4305 f 11*0 7001 4105 14*0 5401 3 7101
  //   4305 f 11*0 7101 4005 14*0 5401 103 7201 4305 10f 11*0 7201 4805 14*0 5401 103 7801 4305 10f 11*0
  //   7801 4205 846*0 5401 104 4301 13*0 5401 10f 1006 104 4301 219*0 5401 104 10f 4301 7 5901 3c01 103
  //   8*0 5901 104 4301 107 12*0 5401 4 7 5901 103 f 10*0 5401 104 7 5901 103 10f 10*0 7 5901 3001 103
  //   12*0 7 5901 3101 103 12*0 7 5901 3201 103 12*0 7 5901 3801 103 12*0 3901 7 5901 103 12*0 7 5901 3a01
  //   103 12*0 5901 107 104 3001 12*0 5901 107 104 3101 12*0 5901 107 104 3201 12*0 5901 107 104 3801 12*0
  //   5901 107 104 3901 12*0 5901 107 104 3a01 668*0 5401 104 10f 5301 104 341 10*0 5021 104 341 13*0 5401
  //   104 10f 7021 305 5701 104 341 8*0 5401 104 10f 5301 3021 103 10*0 5011 3021 103 13*0 5401 104 10f
  //   7011 305 5701 3021 103
endmodule
